# Fritzing sketch Conception Electrique (saved by Fritzing 1.0.6)
breadboards: 1

parts:
  Teensy_3_1 = Teensy 3.1
  Composant1 = INMP441
  Composant2 = BME280 Breakout

nets:
  GND: Teensy_3_1.GND, Composant1.L/R, Composant1.GND, Composant2.GND
  N1: Teensy_3_1.D7, Composant1.SD
  N2: Teensy_3_1.D11, Composant1.WS
  3V3: Teensy_3_1.3V3, Composant1.VDD, Composant2.3.3V
  N3: Teensy_3_1.D13, Composant1.SCK
  N4: Teensy_3_1.A4/D18, Composant2.SDI/SDA
  N5: Teensy_3_1.A5/D19, Composant2.SCK/SCL

custom parts:
  INMP441: This is a simple breakout board for the INMP441 I2S MEMS microphone.
